// Logisim project ObligatorioARQ.circ as structural Verilog: 2 circuits, main circuit main
module main (
  input  [11:0] in_1
);

  wire and_2_out, and_3_out, and_4_out, and_5_out, button_1_out, button_4_out, button_5_out, button_6_out,
       button_7_out, contadortiempo_1_reset, d_ff_1_q, decoder_1_out2, decoder_1_out3, decoder_1_out4,
       decoder_1_out5, not_1_out, or_1_out, RelojMatriz_out, RNG_p1;
  wire [2:0] undriven;
  wire [3:0] contadortiempo_1_mins, contadortiempo_1_segs, contadortiempo_1_segs2;
  wire [11:0] shift_register_1_out, shift_register_2_out, shift_register_3_out, shift_register_4_out;

  D_Flip_Flop d_ff_1 (.Q(d_ff_1_q), .preset(button_1_out), .reset(contadortiempo_1_reset));  // open: D, clk, Qn
  LED led_1 (.in(not_1_out));
  LED led_2 ();  // open: in
  LED led_3 (.in(d_ff_1_q));
  not not_1 (not_1_out, d_ff_1_q);
  Clock RelojMatriz (.out(RelojMatriz_out));
  RAM ram_1 ();  // open: addr, we, oe, clk, din, dout
  // Random #(.width(3)) RNG: pin names not known; wires that end beside it: RNG_p1
  and and_1 (RNG_p1, d_ff_1_q, RelojMatriz_out);
  Decoder #(.select(3)) decoder_1 (
    .out2(decoder_1_out2), .out3(decoder_1_out3), .out4(decoder_1_out4), .out5(decoder_1_out5), .sel(undriven));  // open: out0, out1, out6, out7, en
  Button button_1 (.out(button_1_out));
  Button button_2 ();  // open: out
  Button button_3 ();  // open: out
  Shift_Register #(.length(12)) shift_register_1 (
    .in(decoder_1_out2), .clk(RNG_p1), .out(shift_register_1_out[0]), .clr(contadortiempo_1_reset),
    .q0(shift_register_1_out[11]), .q1(shift_register_1_out[10]), .q2(shift_register_1_out[9]),
    .q3(shift_register_1_out[8]), .q4(shift_register_1_out[7]), .q5(shift_register_1_out[6]),
    .q6(shift_register_1_out[5]), .q7(shift_register_1_out[4]), .q8(shift_register_1_out[3]),
    .q9(shift_register_1_out[2]), .q10(shift_register_1_out[1]));  // open: shift, load, d0, d1, d2, d3, d4, d5, d6, d7, d8, d9, d10, d11, q11
  Shift_Register #(.length(12)) shift_register_2 (
    .in(decoder_1_out3), .clk(RNG_p1), .out(shift_register_2_out[0]), .clr(contadortiempo_1_reset),
    .q0(shift_register_2_out[11]), .q1(shift_register_2_out[10]), .q2(shift_register_2_out[9]),
    .q3(shift_register_2_out[8]), .q4(shift_register_2_out[7]), .q5(shift_register_2_out[6]),
    .q6(shift_register_2_out[5]), .q7(shift_register_2_out[4]), .q8(shift_register_2_out[3]),
    .q9(shift_register_2_out[2]), .q10(shift_register_2_out[1]));  // open: shift, load, d0, d1, d2, d3, d4, d5, d6, d7, d8, d9, d10, d11, q11
  Shift_Register #(.length(12)) shift_register_3 (
    .in(decoder_1_out4), .clk(RNG_p1), .out(shift_register_3_out[0]), .clr(contadortiempo_1_reset),
    .q0(shift_register_3_out[11]), .q1(shift_register_3_out[10]), .q2(shift_register_3_out[9]),
    .q3(shift_register_3_out[8]), .q4(shift_register_3_out[7]), .q5(shift_register_3_out[6]),
    .q6(shift_register_3_out[5]), .q7(shift_register_3_out[4]), .q8(shift_register_3_out[3]),
    .q9(shift_register_3_out[2]), .q10(shift_register_3_out[1]));  // open: shift, load, d0, d1, d2, d3, d4, d5, d6, d7, d8, d9, d10, d11, q11
  Shift_Register #(.length(12)) shift_register_4 (
    .in(decoder_1_out5), .clk(RNG_p1), .out(shift_register_4_out[0]), .clr(contadortiempo_1_reset),
    .q0(shift_register_4_out[11]), .q1(shift_register_4_out[10]), .q2(shift_register_4_out[9]),
    .q3(shift_register_4_out[8]), .q4(shift_register_4_out[7]), .q5(shift_register_4_out[6]),
    .q6(shift_register_4_out[5]), .q7(shift_register_4_out[4]), .q8(shift_register_4_out[3]),
    .q9(shift_register_4_out[2]), .q10(shift_register_4_out[1]));  // open: shift, load, d0, d1, d2, d3, d4, d5, d6, d7, d8, d9, d10, d11, q11
  DotMatrix #(.matrixcols(9), .matrixrows(12)) dotmatrix_1 (
    .col0(in_1), .col1(shift_register_1_out), .col2(in_1), .col3(shift_register_2_out), .col4(in_1),
    .col5(shift_register_3_out), .col6(in_1), .col7(shift_register_4_out), .col8(in_1));
  Hex_Digit_Display hex_digit_display_1 (.value(contadortiempo_1_mins));  // open: dp
  Button button_4 (.out(button_4_out));
  and and_2 (and_2_out, button_4_out, shift_register_1_out[2]);
  and and_3 (and_3_out, button_5_out, shift_register_2_out[2]);
  and and_4 (and_4_out, button_6_out, shift_register_3_out[2]);
  and and_5 (and_5_out, button_7_out, shift_register_4_out[2]);
  Hex_Digit_Display hex_digit_display_2 (.value(contadortiempo_1_segs2));  // open: dp
  Button button_5 (.out(button_5_out));
  Button button_6 (.out(button_6_out));
  Button button_7 (.out(button_7_out));
  Hex_Digit_Display hex_digit_display_3 (.value(contadortiempo_1_segs));  // open: dp
  LED led_4 ();  // open: in
  LED led_5 ();  // open: in
  LED led_6 ();  // open: in
  LED led_7 ();  // open: in
  Counter #(.max('h1f), .width(5)) counter_1 (.clk(or_1_out));  // open: load, D, count, Q, carry, up, clr
  or or_1 (or_1_out, and_2_out, and_3_out, and_4_out, and_5_out);
  LED led_8 ();  // open: in
  LED led_9 ();  // open: in
  LED led_10 ();  // open: in
  LED led_11 ();  // open: in
  ContadorTiempo contadortiempo_1 (
    .in_1(RNG_p1), .Mins(contadortiempo_1_mins), .Segs2(contadortiempo_1_segs2),
    .Segs(contadortiempo_1_segs), .Reset(contadortiempo_1_reset));

  // Notes on the sheet:
  //   Esperando modo
  //   Grabando
  //   Jugando
  //   Grabar
  //   Jugar random
  //   Jugar grabacion
  //   ORTquestra
  //   ____
  //   :
  //   Contador puntos en binario:
endmodule

module ContadorTiempo (
  input  in_1,
  output [3:0] Mins,
  output [3:0] Segs2,
  output [3:0] Segs,
  output Reset
);

  wire and_1_out, clock_1_out, counter_2_carry, counter_3_carry, d_ff_1_q;

  Clock clock_1 (.out(clock_1_out));
  D_Flip_Flop d_ff_1 (.Q(d_ff_1_q), .preset(in_1), .reset(Reset));  // open: D, clk, Qn
  and and_1 (and_1_out, d_ff_1_q, clock_1_out);
  Counter #(.max('h2), .trigger("falling"), .width(4)) counter_1 (
    .clr(Reset), .clk(counter_2_carry), .carry(Reset), .Q(Mins));  // open: load, up, count, D
  Counter #(.max('h5), .trigger("falling"), .width(4)) counter_2 (
    .clr(Reset), .clk(counter_3_carry), .carry(counter_2_carry), .Q(Segs2));  // open: load, up, count, D
  Counter #(.max('h9), .width(4)) counter_3 (
    .clr(Reset), .clk(and_1_out), .carry(counter_3_carry), .Q(Segs));  // open: load, up, count, D
endmodule
